# Fritzing sketch layout (saved by Fritzing 0.9.10b)
perfboards: 1

parts:
  Mod1 = Raspberry Pi Pico W
  HC-SR04_Sensor_1 = HC-SR04 Ultrasonic Distance Sensor
  Battery = male pin header, 2 pins [form="♂ (male)"]
  Motors = male pin header, 2 pins [form="♂ (male)"]
  C1 = Ceramic Capacitor [capacitance=0.1µF voltage=35V package="100 mil [THT, multilayer]"]
  R1 = Resistor [tolerance=±5% power=0.25 resistance=1k package=THT]
  C2 = Electrolytic Capacitor [capacitance=100µF voltage=35V package="100 mil [THT, electrolytic]"]
  IC1 = IC, DIP package, 16 pins [chip_label=3-5v-DC_boost]
  R2 = Resistor [tolerance=±5% power=0.25 resistance=1k package=THT]
  R3 = Resistor [tolerance=±5% power=0.25 resistance=2k package=THT]
  Q2 = NPN-Transistor [package="TO92 [THT]"]
  S1 = Pushbutton [package="[THT]"]
  LED1 = LED - 5mm [color="Red (633nm)" current=0.030 package="5 mm [THT]"]
  R4 = Resistor [tolerance=±5% power=0.25 resistance=1k package=THT]
  R5 = Resistor [tolerance=±5% power=0.25 resistance=100k package=THT]
  Q3 = PNP-Transistor [package="TO92 [THT]"]
  Q4 = PNP-Transistor [package="TO92 [THT]"]
  Q5 = NPN-Transistor [package="TO92 [THT]"]
  Q6 = NPN-Transistor [package="TO92 [THT]"]
  R7 = Resistor [tolerance=±5% power=0.25 resistance=10k package=THT]
  R8 = Resistor [tolerance=±5% power=0.25 resistance=1k package=THT]
  R9 = Resistor [tolerance=±5% power=0.25 resistance=10k package=THT]
  R10 = Resistor [tolerance=±5% power=0.25 resistance=1k package=THT]
  Q7 = NPN-Transistor [package="TO92 [THT]"]
  R11 = Resistor [tolerance=±5% power=0.25 resistance=100k package=THT]

nets:
  N1: Mod1.pin_3, Mod1.pin_8, Mod1.pin_13, Mod1.pin_18, Mod1.pin_23, Mod1.pin_28, Mod1.pin_33, Mod1.pin_38
  N2: Mod1.pin_15, R10.Pin_0
  N3: Mod1.pin_17, Q2.B
  N4: Mod1.pin_19, HC-SR04_Sensor_1.TRIG
  N5: Mod1.pin_20, R2.Pin_1, R3.Pin_0
  N6: Mod1.pin_21, Mod1.pin_36, S1.Pin_1, S1.Pin_2, S1.Pin_3, S1.Pin_4
  N7: Mod1.pin_22, Q5.B
  N8: Mod1.pin_24, Q6.B
  N9: Mod1.pin_25, R1.Pin_1
  N10: Mod1.pin_31, R5.Pin_1, R11.Pin_0
  N11: HC-SR04_Sensor_1.VCC, C2.-, IC1.pin9, R7.Pin_0
  N12: HC-SR04_Sensor_1.ECHO, R2.Pin_0
  N13: HC-SR04_Sensor_1.GND, Q2.C
  N14: Battery.pin1, C1.0, LED1.cathode, R5.Pin_0, Q7.E
  N15: Battery.pin2, C1.1, IC1.pin1, R11.Pin_1
  N16: Motors.pin1, Q4.E
  N17: Motors.pin2, Q3.E
  N18: R1.Pin_0, LED1.anode
  N19: C2.+, IC1.pin8
  N20: IC1.pin16, Q7.C
  N21: R4.Pin_0, Q3.B, R7.Pin_1
  N22: R4.Pin_1, Q5.C
  N23: Q4.B, R8.Pin_0, R9.Pin_1
  N24: Q6.C, R8.Pin_1
  N25: R10.Pin_1, Q7.B

notes:
  Green - Motor UP
  White - Motor Down
  Orange - Sensor Receive
  Gray - Sensor read request
  Purple - Enable 5V boost
  Yellow - ADC
  Brown - Join point
  R1 = R2 = R4 = R8 = R10 = 1K
  R3 = 2K, R5 = R6 = 100K, R7 = R9 = 10K
  Q1 = Q2 = Q3 = Q6 = S8050
  Q4 = Q5 = S8550

custom parts:
  Raspberry Pi Pico W: Raspberry Pi Pico W. Based around the RP2040 microcontroller the Pico W is a low cost microcontroller device bringing Raspberry Pi quality, cost, and easy of use to the microcontroller space. The areas marked KEEPOUT in pcb silkscreen should not have traces running through them to avoid shorts on a soldered in module!
